// Logisim project HW_B1_RDBL12_DaoVanQuyet.circ as structural Verilog: 2 circuits, main circuit AsynUpCounter
module AsynUpCounter (
);

  wire clock_1_out, clock_2_out, d_ff_1_qn, d_ff_3_qn, d_ff_5_qn, d_ff_7_qn;
  wire [3:0] d_ff_1_q, d_ff_2_qn;

  Clock clock_1 (.out(clock_1_out));
  Clock clock_2 (.out(clock_2_out));
  D_Flip_Flop d_ff_1 (.D(d_ff_1_qn), .clk(clock_1_out), .Q(d_ff_1_q[0]), .Qn(d_ff_1_qn));  // open: preset, reset
  D_Flip_Flop d_ff_2 (.D(d_ff_2_qn[0]), .clk(clock_2_out), .Qn(d_ff_2_qn[0]));  // open: Q, preset, reset
  D_Flip_Flop d_ff_3 (.D(d_ff_3_qn), .clk(d_ff_1_qn), .Q(d_ff_1_q[1]), .Qn(d_ff_3_qn));  // open: preset, reset
  D_Flip_Flop d_ff_4 (.D(d_ff_2_qn[1]), .clk(d_ff_2_qn[0]), .Qn(d_ff_2_qn[1]));  // open: Q, preset, reset
  Hex_Digit_Display hex_digit_display_1 (.value(d_ff_1_q));  // open: dp
  Hex_Digit_Display hex_digit_display_2 (.value(d_ff_2_qn));  // open: dp
  D_Flip_Flop d_ff_5 (.D(d_ff_5_qn), .clk(d_ff_3_qn), .Q(d_ff_1_q[2]), .Qn(d_ff_5_qn));  // open: preset, reset
  D_Flip_Flop d_ff_6 (.D(d_ff_2_qn[2]), .clk(d_ff_2_qn[1]), .Qn(d_ff_2_qn[2]));  // open: Q, preset, reset
  D_Flip_Flop d_ff_7 (.D(d_ff_7_qn), .clk(d_ff_5_qn), .Q(d_ff_1_q[3]), .Qn(d_ff_7_qn));  // open: preset, reset
  D_Flip_Flop d_ff_8 (.D(d_ff_2_qn[3]), .clk(d_ff_2_qn[2]), .Qn(d_ff_2_qn[3]));  // open: Q, preset, reset

  // Notes on the sheet:
  //   ASYN UP COUNTER
  //   ASYN DOWN COUNTER
endmodule

module AsynDownCounter (
);

  wire clock_1_out;
  wire [3:0] d_ff_1_qn;

  Clock clock_1 (.out(clock_1_out));
  D_Flip_Flop d_ff_1 (.D(d_ff_1_qn[0]), .clk(clock_1_out), .Qn(d_ff_1_qn[0]));  // open: Q, preset, reset
  D_Flip_Flop d_ff_2 (.D(d_ff_1_qn[1]), .clk(d_ff_1_qn[0]), .Qn(d_ff_1_qn[1]));  // open: Q, preset, reset
  Hex_Digit_Display hex_digit_display_1 (.value(d_ff_1_qn));  // open: dp
  D_Flip_Flop d_ff_3 (.D(d_ff_1_qn[2]), .clk(d_ff_1_qn[1]), .Qn(d_ff_1_qn[2]));  // open: Q, preset, reset
  D_Flip_Flop d_ff_4 (.D(d_ff_1_qn[3]), .clk(d_ff_1_qn[2]), .Qn(d_ff_1_qn[3]));  // open: Q, preset, reset
endmodule
